# Fritzing sketch PanelLED_wiring (saved by Fritzing 0.9.3b)

parts:
  WeMos_D1_R1 = WeMos D1 R2
  NEOPIXEL1 = Neopixel Strip -- White (60/m)
  JACK1 = 2.1mm Barrel Jack with Terminal Block

nets:
  N1: WeMos_D1_R1.D9, NEOPIXEL1.+5V
  N2: WeMos_D1_R1.5V, NEOPIXEL1.DI, JACK1.POS
  N3: NEOPIXEL1.GND, JACK1.NEG

custom parts:
  WeMos D1 R2: The D1 R2 is a mini wifi board based on the ESP-8266EX.
  Neopixel Strip -- White (60/m): Neopixel Strip, White, 60 pixels per meter.
